// Logisim project processor.circ as structural Verilog: 6 circuits, main circuit Datapath
module main (
  input  in_1,
  output [3:0] out_2,
  output [2:0] A1,
  output [31:0] WD3,
  output [2:0] A2,
  output [2:0] F,
  output [31:0] A,
  output [31:0] Y,
  output [2:0] A3,
  output [31:0] B,
  output [31:0] V0,
  output [6:0] out_12,
  output [31:0] B_2,
  output [6:0] out_14,
  output [2:0] A3_2
);

  wire alu_1_zero, and_1_out, clock_1_out, controlunit_1_alusrc, controlunit_1_branch, controlunit_1_regdst,
       controlunit_1_regwrite;
  wire [7:0] adder_1_out, adder_2_out, bitselector_7_out, multiplexer_1_out, multiplexer_4_out, PC_q,
       shifter_2_out, shifter_3_out;
  wire [15:0] bitselector_4_out;
  wire [31:0] multiplexer_3_out, rom_1_data;

  Multiplexer #(.width(8), .enable("false")) multiplexer_1 (
    .in0(multiplexer_4_out), .in1({8{1'b0}}), .out(multiplexer_1_out), .sel(in_1));
  BitSelector #(.width(32), .group(7)) bitselector_1 (.in(rom_1_data), .out(out_12), .sel(3'b001));
  Clock clock_1 (.out(clock_1_out));
  Register PC (.D(multiplexer_1_out), .Q(PC_q), .clk(clock_1_out));  // open: en, clr
  Adder adder_1 (.a(PC_q), .b(8'h4), .out(adder_1_out));  // open: cin, cout
  Multiplexer #(.width(3), .enable("false")) multiplexer_2 (.in0(A2), .in1(A3_2), .out(A3), .sel(controlunit_1_regdst));
  Shifter #(.width(7), .shift("lr")) shifter_1 (.in(out_12), .\dist (3'b100), .out(out_14));
  BitSelector #(.width(7), .group(3)) bitselector_2 (.in(out_14), .out(A3_2), .sel(2'b00));
  Shifter #(.shift("lr")) shifter_2 (.in(PC_q), .\dist (3'b010), .out(shifter_2_out));
  ROM #(.dataWidth(32)) rom_1 (.addr(shifter_2_out), .data(rom_1_data));  // open: sel
  ROM #(.dataWidth(32)) rom_2 (.data(rom_1_data));  // open: addr, sel
  BitSelector #(.width(32), .group(3)) bitselector_3 (.in(rom_1_data), .out(A1), .sel(4'b0111));
  RegisterFile registerfile_1 (
    .CLK(clock_1_out), .A1(A1), .WD3(WD3), .A2(A2), .WE3(controlunit_1_regwrite), .RD1(A), .RD2(B), .A3(A3),
    .V0(V0));
  ControlUnit controlunit_1 (
    .Instruction(rom_1_data), .RegDst(controlunit_1_regdst), .RegWrite(controlunit_1_regwrite),
    .ALUControl(F), .Branch(controlunit_1_branch), .ALUSrc(controlunit_1_alusrc));
  BitSelector #(.width(32), .group(16)) bitselector_4 (.in(rom_1_data), .out(bitselector_4_out), .sel(1'b0));
  BitSelector #(.width(32), .group(4)) bitselector_5 (.in(rom_1_data), .out(out_2), .sel(3'b100));
  BitSelector #(.width(4), .group(3)) bitselector_6 (.in(out_2), .out(A2), .sel(1'b0));
  assign B_2 = {{16{bitselector_4_out[15]}}, bitselector_4_out};  // Bit_Extender bit_extender_1
  BitSelector #(.width(16), .group(8)) bitselector_7 (.in(bitselector_4_out), .out(bitselector_7_out), .sel(1'b0));
  Multiplexer #(.width(32), .enable("false")) multiplexer_3 (
    .in0(B), .in1(B_2), .out(multiplexer_3_out), .sel(controlunit_1_alusrc));
  ALU alu_1 (.F(F), .Y(WD3), .B(multiplexer_3_out), .A(A), .Zero(alu_1_zero));
  Multiplexer #(.width(8), .enable("false")) multiplexer_4 (
    .in0(adder_1_out), .in1(adder_2_out), .out(multiplexer_4_out), .sel(and_1_out));
  Shifter shifter_3 (.in(bitselector_7_out), .\dist (3'b010), .out(shifter_3_out));
  Adder adder_2 (.a(shifter_3_out), .b(adder_1_out), .out(adder_2_out));  // open: cin, cout
  and and_1 (and_1_out, controlunit_1_branch, alu_1_zero);

  assign Y = WD3;

  // Notes on the sheet:
  //   contents of rom_1 (hex, n*v repeats v):
  //   20040004 1020 10800012 20 20020001 1082000f 20 20630001 20050000 20060000 c23020 20a50001 10a30003
  //   20 1000fffb 20 20c20000 10830003 20 1000fff3 20 20 1000fffe 20
  //   contents of rom_2 (hex, n*v repeats v):
  //   20040004 1020 1080000b 20 20020001 20030001 10820007 20 20630001 70621002 10830003 20 1000fffb 20 20
  //   1000fffe 20
endmodule

module ALU (
  input  [2:0] F,
  input  [31:0] B,
  input  [31:0] A,
  output Zero,
  output [31:0] Y
);

  wire adder_1_cout, bitselector_1_out;
  wire [31:0] adder_1_out, and_1_out, bit_extender_1_out, multiplexer_1_out, multiplier_1_out, not_1_out,
       or_1_out;

  assign not_1_out = ~B;  // NOT_Gate not_1, 32 bits wide
  Multiplexer #(.width(32), .enable("false")) multiplexer_1 (
    .in0(B), .in1(not_1_out), .out(multiplexer_1_out), .sel(F[2]));
  assign and_1_out = B & A;  // AND_Gate and_1, 32 bits wide
  assign or_1_out = B | A;  // OR_Gate or_1, 32 bits wide
  Adder #(.width(32)) adder_1 (.a(multiplexer_1_out), .b(A), .out(adder_1_out), .cin(F[2]), .cout(adder_1_cout));
  Multiplier #(.width(32)) multiplier_1 (.a(B), .b(A), .out(multiplier_1_out));  // open: cin, cout
  BitSelector #(.width(32)) bitselector_1 (.in(adder_1_out), .out(bitselector_1_out), .sel({5{1'b1}}));
  assign bit_extender_1_out = {{31{bitselector_1_out}}, bitselector_1_out};  // Bit_Extender bit_extender_1
  Multiplexer #(.select(3), .width(32), .enable("false")) multiplexer_2 (
    .in0(and_1_out), .in1(or_1_out), .in2(adder_1_out), .in3(multiplier_1_out), .in6(adder_1_out),
    .in7(bit_extender_1_out), .out(Y), .sel(F));  // open: in4, in5
  nor nor_1 (Zero, Y[0], Y[1], Y[2], Y[3], Y[4], Y[5], Y[6], Y[7], Y[8], Y[9], Y[10], Y[11], Y[12], Y[13], Y[14], Y[15], Y[17], Y[18], Y[19], Y[20], Y[21], Y[22], Y[23], Y[24], Y[25], Y[26], Y[27], Y[28], Y[29], Y[30], Y[31], Y[16]);
endmodule

module Datapath (
  input  in_1,
  output [3:0] out_2,
  output [2:0] A1,
  output [31:0] WD3,
  output [2:0] A2,
  output [2:0] F,
  output [31:0] A,
  output [2:0] A3,
  output [31:0] Y,
  output [31:0] V0,
  output [31:0] B,
  output [6:0] out_12,
  output [31:0] B_2,
  output [6:0] out_14,
  output [2:0] A3_2
);

  wire adder_2_cout, and_1_out, and_2_out, and_3_out, and_4_out, and_5_out, and_6_out, and_7_out, and_9_out,
       bitselector_8_out, clock_1_out, controlunit_1_alusrc, controlunit_1_branch, controlunit_1_regdst,
       controlunit_1_regwrite, decoder_1_out0, decoder_1_out1, decoder_1_out2, decoder_1_out3,
       decoder_1_out4, decoder_1_out5, decoder_1_out6, decoder_1_out7, nor_1_out;
  wire [7:0] adder_1_out, adder_3_out, bitselector_7_out, multiplexer_1_out, multiplexer_8_out, PC_q,
       shifter_2_out, shifter_3_out;
  wire [15:0] bitselector_4_out;
  wire [31:0] adder_2_out, and_8_out, bit_extender_2_out, multiplexer_5_out, multiplexer_6_out, not_1_out,
       or_1_out, register_1_q, register_2_q, register_4_q, register_5_q, register_6_q, register_7_q,
       register_8_q, rom_1_data;

  Multiplexer #(.width(8), .enable("false")) multiplexer_1 (
    .in0(multiplexer_8_out), .in1({8{1'b0}}), .out(multiplexer_1_out), .sel(in_1));
  BitSelector #(.width(32), .group(7)) bitselector_1 (.in(rom_1_data), .out(out_12), .sel(3'b001));
  Clock clock_1 (.out(clock_1_out));
  Register PC (.D(multiplexer_1_out), .Q(PC_q), .clk(clock_1_out));  // open: en, clr
  Adder adder_1 (.a(PC_q), .b(8'h4), .out(adder_1_out));  // open: cin, cout
  Decoder #(.select(3), .enable("false")) decoder_1 (
    .out0(decoder_1_out0), .out1(decoder_1_out1), .out2(decoder_1_out2), .out3(decoder_1_out3),
    .out4(decoder_1_out4), .out5(decoder_1_out5), .out6(decoder_1_out6), .out7(decoder_1_out7), .sel(A3));
  Multiplexer #(.width(3), .enable("false")) multiplexer_2 (.in0(A2), .in1(A3_2), .out(A3), .sel(controlunit_1_regdst));
  Shifter #(.width(7), .shift("lr")) shifter_1 (.in(out_12), .\dist (3'b100), .out(out_14));
  BitSelector #(.width(7), .group(3)) bitselector_2 (.in(out_14), .out(A3_2), .sel(2'b00));
  Shifter #(.shift("lr")) shifter_2 (.in(PC_q), .\dist (3'b010), .out(shifter_2_out));
  and and_1 (and_1_out, controlunit_1_regwrite, decoder_1_out1);
  and and_2 (and_2_out, controlunit_1_regwrite, decoder_1_out2);
  and and_3 (and_3_out, controlunit_1_regwrite, decoder_1_out3);
  and and_4 (and_4_out, controlunit_1_regwrite, decoder_1_out4);
  and and_5 (and_5_out, controlunit_1_regwrite, decoder_1_out5);
  and and_6 (and_6_out, controlunit_1_regwrite, decoder_1_out6);
  and and_7 (and_7_out, controlunit_1_regwrite, decoder_1_out7);
  ROM #(.dataWidth(32)) rom_1 (.addr(shifter_2_out), .data(rom_1_data));  // open: sel
  Register #(.width(32)) register_1 (.D({32{1'b0}}), .Q(register_1_q), .clk(clock_1_out));  // open: en, clr
  Register #(.width(32)) register_2 (.D(WD3), .en(and_1_out), .Q(register_2_q), .clk(clock_1_out));  // open: clr
  Register #(.width(32)) register_3 (.D(WD3), .en(and_2_out), .Q(V0), .clk(clock_1_out));  // open: clr
  Register #(.width(32)) register_4 (.D(WD3), .en(and_3_out), .Q(register_4_q), .clk(clock_1_out));  // open: clr
  Register #(.width(32)) register_5 (.D(WD3), .en(and_4_out), .Q(register_5_q), .clk(clock_1_out));  // open: clr
  Register #(.width(32)) register_6 (.D(WD3), .en(and_5_out), .Q(register_6_q), .clk(clock_1_out));  // open: clr
  Register #(.width(32)) register_7 (.D(WD3), .en(and_6_out), .Q(register_7_q), .clk(clock_1_out));  // open: clr
  Register #(.width(32)) register_8 (.D(WD3), .en(and_7_out), .Q(register_8_q), .clk(clock_1_out));  // open: clr
  BitSelector #(.width(32), .group(3)) bitselector_3 (.in(rom_1_data), .out(A1), .sel(4'b0111));
  ControlUnit controlunit_1 (
    .Instruction(rom_1_data), .RegDst(controlunit_1_regdst), .RegWrite(controlunit_1_regwrite),
    .ALUControl(F), .Branch(controlunit_1_branch), .ALUSrc(controlunit_1_alusrc));
  Multiplexer #(.select(3), .width(32), .enable("false")) multiplexer_3 (
    .in0(register_1_q), .in1(register_2_q), .in2(V0), .in3(register_4_q), .in4(register_5_q),
    .in5(register_6_q), .in6(register_7_q), .in7(register_8_q), .out(A), .sel(A1));
  Multiplexer #(.select(3), .width(32), .enable("false")) multiplexer_4 (
    .in0(register_1_q), .in1(register_2_q), .in2(V0), .in3(register_4_q), .in4(register_5_q),
    .in5(register_6_q), .in6(register_7_q), .in7(register_8_q), .out(B), .sel(A2));
  BitSelector #(.width(32), .group(16)) bitselector_4 (.in(rom_1_data), .out(bitselector_4_out), .sel(1'b0));
  BitSelector #(.width(32), .group(4)) bitselector_5 (.in(rom_1_data), .out(out_2), .sel(3'b100));
  BitSelector #(.width(4), .group(3)) bitselector_6 (.in(out_2), .out(A2), .sel(1'b0));
  assign B_2 = {{16{bitselector_4_out[15]}}, bitselector_4_out};  // Bit_Extender bit_extender_1
  BitSelector #(.width(16), .group(8)) bitselector_7 (.in(bitselector_4_out), .out(bitselector_7_out), .sel(1'b0));
  Multiplexer #(.width(32), .enable("false")) multiplexer_5 (
    .in0(B), .in1(B_2), .out(multiplexer_5_out), .sel(controlunit_1_alusrc));
  Multiplexer #(.width(32), .enable("false")) multiplexer_6 (
    .in0(multiplexer_5_out), .in1(not_1_out), .out(multiplexer_6_out), .sel(F[2]));
  assign not_1_out = ~multiplexer_5_out;  // NOT_Gate not_1, 32 bits wide
  assign and_8_out = multiplexer_5_out & A;  // AND_Gate and_8, 32 bits wide
  assign or_1_out = multiplexer_5_out | A;  // OR_Gate or_1, 32 bits wide
  Adder #(.width(32)) adder_2 (.a(multiplexer_6_out), .b(A), .out(adder_2_out), .cin(F[2]), .cout(adder_2_cout));
  BitSelector #(.width(32)) bitselector_8 (.in(adder_2_out), .out(bitselector_8_out), .sel({5{1'b1}}));
  assign bit_extender_2_out = {{31{bitselector_8_out}}, bitselector_8_out};  // Bit_Extender bit_extender_2
  Multiplexer #(.select(3), .width(32), .enable("false")) multiplexer_7 (
    .in0(and_8_out), .in1(or_1_out), .in2(adder_2_out), .in6(adder_2_out), .in7(bit_extender_2_out),
    .out(WD3), .sel(F));  // open: in3, in4, in5
  Multiplexer #(.width(8), .enable("false")) multiplexer_8 (
    .in0(adder_1_out), .in1(adder_3_out), .out(multiplexer_8_out), .sel(and_9_out));
  Shifter shifter_3 (.in(bitselector_7_out), .\dist (3'b010), .out(shifter_3_out));
  Adder adder_3 (.a(shifter_3_out), .b(adder_1_out), .out(adder_3_out));  // open: cin, cout
  nor nor_1 (nor_1_out, WD3[0], WD3[1], WD3[2], WD3[3], WD3[4], WD3[5], WD3[6], WD3[7], WD3[8], WD3[9], WD3[10], WD3[11], WD3[12], WD3[13], WD3[14], WD3[15], WD3[17], WD3[18], WD3[19], WD3[20], WD3[21], WD3[22], WD3[23], WD3[24], WD3[25], WD3[26], WD3[27], WD3[28], WD3[29], WD3[30], WD3[31], WD3[16]);
  and and_9 (and_9_out, controlunit_1_branch, nor_1_out);

  assign Y = WD3;

  // Notes on the sheet:
  //   contents of rom_1 (hex, n*v repeats v):
  //   20040004 1020 10800012 20 20020001 1082000f 20 20630001 20050000 20060000 c23020 20a50001 10a30003
  //   20 1000fffb 20 20c20000 10830003 20 1000fff3 20 20 1000fffe 20
endmodule

module Tests (
  output [31:0] Y,
  output [7:0] out_2,
  output [7:0] out_3,
  output [2:0] out_4
);

  BitSelector #(.width(32), .group(8)) bitselector_1 (.in(32'h12356789), .out(out_2), .sel(2'b01));
  BitSelector #(.width(32), .group(8)) bitselector_2 (.in(32'h12356789), .out(out_3), .sel(2'b01));
  BitSelector #(.group(3)) bitselector_3 (.in(out_3), .out(out_4), .sel(2'b00));

  assign Y = 32'hf4010207;

  // Notes on the sheet:
  //   binary values in Logisim. Convince yourself how the bits are displayed.
  //   Example 2: The bit selector is configured to have 32  
  //   bit group #1 (starting at index 0) is selected for the output.
  //   That is, the 8 bits 0x67 at bit indices 15..8  are sent to the output.
  //   Example 3: Now, assume that you want to extract 3 bits at   
  //   Example 1: A simple example that illustrates how 32-bit values are displayed as 
  //   input bits and 8 output bits. The parameter constant is 1, which means that   
  //   bit indices 10..8. This can be accoplished by putting two bit selecotrs in series.
endmodule

module RegisterFile (
  input  CLK,
  input  [2:0] A1,
  input  [31:0] WD3,
  input  [2:0] A2,
  input  WE3,
  input  [2:0] A3,
  output [31:0] RD1,
  output [31:0] RD2,
  output [31:0] V0
);

  wire and_1_out, and_2_out, and_3_out, and_4_out, and_5_out, and_6_out, and_7_out, decoder_1_out0,
       decoder_1_out1, decoder_1_out2, decoder_1_out3, decoder_1_out4, decoder_1_out5, decoder_1_out6,
       decoder_1_out7;
  wire [31:0] register_1_q, register_2_q, register_4_q, register_5_q, register_6_q, register_7_q,
       register_8_q;

  Decoder #(.select(3)) decoder_1 (
    .out0(decoder_1_out0), .out1(decoder_1_out1), .out2(decoder_1_out2), .out3(decoder_1_out3),
    .out4(decoder_1_out4), .out5(decoder_1_out5), .out6(decoder_1_out6), .out7(decoder_1_out7), .sel(A3));  // open: en
  and and_1 (and_1_out, WE3, decoder_1_out1);
  and and_2 (and_2_out, WE3, decoder_1_out2);
  and and_3 (and_3_out, WE3, decoder_1_out3);
  and and_4 (and_4_out, WE3, decoder_1_out4);
  and and_5 (and_5_out, WE3, decoder_1_out5);
  and and_6 (and_6_out, WE3, decoder_1_out6);
  and and_7 (and_7_out, WE3, decoder_1_out7);
  Register #(.width(32)) register_1 (.D({32{1'b0}}), .Q(register_1_q), .clk(CLK));  // open: en, clr
  Register #(.width(32)) register_2 (.D(WD3), .en(and_1_out), .Q(register_2_q), .clk(CLK));  // open: clr
  Register #(.width(32)) register_3 (.D(WD3), .en(and_2_out), .Q(V0), .clk(CLK));  // open: clr
  Register #(.width(32)) register_4 (.D(WD3), .en(and_3_out), .Q(register_4_q), .clk(CLK));  // open: clr
  Register #(.width(32)) register_5 (.D(WD3), .en(and_4_out), .Q(register_5_q), .clk(CLK));  // open: clr
  Register #(.width(32)) register_6 (.D(WD3), .en(and_5_out), .Q(register_6_q), .clk(CLK));  // open: clr
  Register #(.width(32)) register_7 (.D(WD3), .en(and_6_out), .Q(register_7_q), .clk(CLK));  // open: clr
  Register #(.width(32)) register_8 (.D(WD3), .en(and_7_out), .Q(register_8_q), .clk(CLK));  // open: clr
  Multiplexer #(.select(3), .width(32)) multiplexer_1 (
    .in0(register_1_q), .in1(register_2_q), .in2(V0), .in3(register_4_q), .in4(register_5_q),
    .in5(register_6_q), .in6(register_7_q), .in7(register_8_q), .out(RD1), .sel(A1));  // open: en
  Multiplexer #(.select(3), .width(32)) multiplexer_2 (
    .in0(register_1_q), .in1(register_2_q), .in2(V0), .in3(register_4_q), .in4(register_5_q),
    .in5(register_6_q), .in6(register_7_q), .in7(register_8_q), .out(RD2), .sel(A2));  // open: en
endmodule

module ControlUnit (
  input  [31:0] Instruction,
  output RegDst,
  output RegWrite,
  output ALUSrc,
  output Branch,
  output [2:0] ALUControl
);

  wire comparator_2_eq, comparator_4_eq;
  wire [2:0] multiplexer_1_out;
  wire [5:0] bitselector_1_out;
  wire [31:0] shifter_1_out;

  Shifter #(.width(32), .shift("lr")) shifter_1 (.in(Instruction), .\dist (5'b11010), .out(shifter_1_out));
  BitSelector #(.width(32), .group(6)) bitselector_1 (.in(shifter_1_out), .out(bitselector_1_out), .sel(3'b000));
  Comparator #(.width(6), .mode("unsigned")) comparator_1 (
    .a(bitselector_1_out), .b(6'b001000), .eq(ALUSrc));  // open: gt, lt
  Comparator #(.width(6), .mode("unsigned")) comparator_2 (
    .a(bitselector_1_out), .b({6{1'b0}}), .eq(comparator_2_eq));  // open: gt, lt
  Comparator #(.width(6), .mode("unsigned")) comparator_3 (
    .a(bitselector_1_out), .b(6'b000100), .eq(Branch));  // open: gt, lt
  Multiplexer #(.width(3), .enable("false")) multiplexer_1 (
    .in0(3'b010), .in1(3'b110), .out(multiplexer_1_out), .sel(Branch));
  Comparator #(.width(6), .mode("unsigned")) comparator_4 (
    .a(bitselector_1_out), .b(6'b011100), .eq(comparator_4_eq));  // open: gt, lt
  Multiplexer #(.width(3), .enable("false")) multiplexer_2 (
    .in0(multiplexer_1_out), .in1(3'b011), .out(ALUControl), .sel(comparator_4_eq));
  or or_1 (RegWrite, ALUSrc, comparator_4_eq, comparator_2_eq);
  or or_2 (RegDst, comparator_4_eq, comparator_2_eq);
endmodule
