// Logisim project processor.circ as structural Verilog
module ALU (
  input  [2:0] F,
  input  [31:0] B,
  input  [31:0] A,
  output ZERO,
  output [31:0] Y
);

  wire adder_1_cout, bitselector_1_out;
  wire [31:0] adder_1_out, and_1_out, bit_extender_1_out, multiplexer_1_out, not_1_out, or_1_out;

  assign not_1_out = ~B;  // NOT_Gate not_1, 32 bits wide
  Multiplexer #(.width(32), .enable("false")) multiplexer_1 (
    .in0(B), .in1(not_1_out), .out(multiplexer_1_out), .sel(F[0]));
  assign and_1_out = B & A;  // AND_Gate and_1, 32 bits wide
  assign or_1_out = B | A;  // OR_Gate or_1, 32 bits wide
  Adder #(.width(32)) adder_1 (.a(multiplexer_1_out), .b(A), .out(adder_1_out), .cin(F[0]), .cout(adder_1_cout));
  BitSelector #(.width(32)) bitselector_1 (.in(adder_1_out), .out(bitselector_1_out), .sel({5{1'b1}}));
  assign bit_extender_1_out = {{31{bitselector_1_out}}, bitselector_1_out};  // Bit_Extender bit_extender_1
  Multiplexer #(.select(3), .width(32), .enable("false")) multiplexer_2 (
    .in0(and_1_out), .in1(or_1_out), .in2(adder_1_out), .in6(adder_1_out), .in7(bit_extender_1_out), .out(Y),
    .sel(F));  // open: in3, in4, in5
  // NOR_Gate nor_1 has open pins: in0=Y[0], in1=Y[1], in2=Y[2], in3=Y[3], in4=Y[4], in5=Y[5], in6=Y[6], in7=Y[7], in8=Y[8], in9=Y[9], in10=Y[10], in11=Y[11], in12=Y[12], in13=Y[13], in14=Y[14], in15=Y[15], in16=Y[17], in17=Y[18], in18=Y[19], in19=Y[20], in20=Y[21], in21=Y[22], in22=Y[23], in23=Y[24], in24=Y[25], in25=Y[26], in26=Y[27], in27=Y[28], in28=Y[29], in29=Y[30], in30=Y[31], in31=Y[16], out=open
endmodule

module Datapath (
  input  in_1,
  input  [31:0] WD3,
  output [31:0] v0,
  output [3:0] out_4,
  output [2:0] A1,
  output [2:0] A2,
  output [31:0] RD1,
  output [6:0] out_8,
  output [31:0] RD2,
  output [2:0] A3,
  output [6:0] out_11,
  output [31:0] V0_2
);

  wire and_1_out, and_2_out, and_3_out, and_4_out, and_5_out, and_6_out, and_7_out, clock_1_out,
       controlunit_1_regwrite, decoder_1_out0, decoder_1_out1, decoder_1_out2, decoder_1_out3,
       decoder_1_out4, decoder_1_out5, decoder_1_out6, decoder_1_out7;
  wire [7:0] adder_1_out, multiplexer_1_out, PC_q, shifter_2_out;
  wire [31:0] register_1_q, register_2_q, register_4_q, register_5_q, register_6_q, register_7_q,
       register_8_q, rom_1_data;

  Multiplexer #(.width(8), .enable("false")) multiplexer_1 (
    .in0(adder_1_out), .in1({8{1'b0}}), .out(multiplexer_1_out), .sel(in_1));
  BitSelector #(.width(32), .group(7)) bitselector_1 (.in(32'h851820), .out(out_8), .sel(3'b001));
  Clock clock_1 (.out(clock_1_out));
  Register PC (.D(multiplexer_1_out), .Q(PC_q), .clk(clock_1_out));  // open: en, clr
  Adder adder_1 (.a(PC_q), .b(8'h4), .out(adder_1_out));  // open: cin, cout
  Decoder #(.select(3)) decoder_1 (
    .out0(decoder_1_out0), .out1(decoder_1_out1), .out2(decoder_1_out2), .out3(decoder_1_out3),
    .out4(decoder_1_out4), .out5(decoder_1_out5), .out6(decoder_1_out6), .out7(decoder_1_out7), .sel(A3));  // open: en
  Shifter #(.width(7), .shift("lr")) shifter_1 (.in(out_8), .\dist (3'b100), .out(out_11));
  BitSelector #(.width(7), .group(3)) bitselector_2 (.in(out_11), .out(A3), .sel(2'b00));
  Shifter #(.shift("lr")) shifter_2 (.in(PC_q), .\dist (3'b010), .out(shifter_2_out));
  and and_1 (and_1_out, controlunit_1_regwrite, decoder_1_out1);
  and and_2 (and_2_out, controlunit_1_regwrite, decoder_1_out2);
  and and_3 (and_3_out, controlunit_1_regwrite, decoder_1_out3);
  and and_4 (and_4_out, controlunit_1_regwrite, decoder_1_out4);
  and and_5 (and_5_out, controlunit_1_regwrite, decoder_1_out5);
  and and_6 (and_6_out, controlunit_1_regwrite, decoder_1_out6);
  and and_7 (and_7_out, controlunit_1_regwrite, decoder_1_out7);
  ROM #(.dataWidth(32)) rom_1 (.addr(shifter_2_out), .data(rom_1_data));  // open: sel
  Register #(.width(32)) register_1 (.D({32{1'b0}}), .Q(register_1_q), .clk(clock_1_out));  // open: en, clr
  Register #(.width(32)) register_2 (.D(WD3), .en(and_1_out), .Q(register_2_q), .clk(clock_1_out));  // open: clr
  Register #(.width(32)) register_3 (.D(WD3), .en(and_2_out), .Q(V0_2), .clk(clock_1_out));  // open: clr
  Register #(.width(32)) register_4 (.D(WD3), .en(and_3_out), .Q(register_4_q), .clk(clock_1_out));  // open: clr
  Register #(.width(32)) register_5 (.D(WD3), .en(and_4_out), .Q(register_5_q), .clk(clock_1_out));  // open: clr
  Register #(.width(32)) register_6 (.D(WD3), .en(and_5_out), .Q(register_6_q), .clk(clock_1_out));  // open: clr
  Register #(.width(32)) register_7 (.D(WD3), .en(and_6_out), .Q(register_7_q), .clk(clock_1_out));  // open: clr
  Register #(.width(32)) register_8 (.D(WD3), .en(and_7_out), .Q(register_8_q), .clk(clock_1_out));  // open: clr
  BitSelector #(.width(32), .group(3)) bitselector_3 (.in(32'h851820), .out(A1), .sel(4'b0111));
  ControlUnit controlunit_1 (
    .Instruction(rom_1_data), .RegWrite(controlunit_1_regwrite));  // open: RegDst, ALUControl, Branch, ALUSrc
  Multiplexer #(.select(3), .width(32)) multiplexer_2 (
    .in0(register_1_q), .in1(register_2_q), .in2(V0_2), .in3(register_4_q), .in4(register_5_q),
    .in5(register_6_q), .in6(register_7_q), .in7(register_8_q), .out(RD1), .sel(A1));  // open: en
  Multiplexer #(.select(3), .width(32)) multiplexer_3 (
    .in0(register_1_q), .in1(register_2_q), .in2(V0_2), .in3(register_4_q), .in4(register_5_q),
    .in5(register_6_q), .in6(register_7_q), .in7(register_8_q), .out(RD2), .sel(A2));  // open: en
  BitSelector #(.width(32), .group(4)) bitselector_4 (.in(32'h851820), .out(out_4), .sel(3'b100));
  BitSelector #(.width(4), .group(3)) bitselector_5 (.in(out_4), .out(A2), .sel(1'b0));

  assign v0 = 32'h851820;

  // Notes on the sheet:
  //   contents of rom_1 (hex, n*v repeats v):
  //   20040004 20820002
endmodule

module Tests (
  output [31:0] Y,
  output [7:0] out_2,
  output [7:0] out_3,
  output [2:0] out_4
);

  BitSelector #(.width(32), .group(8)) bitselector_1 (.in(32'h12356789), .out(out_2), .sel(2'b01));
  BitSelector #(.width(32), .group(8)) bitselector_2 (.in(32'h12356789), .out(out_3), .sel(2'b01));
  BitSelector #(.group(3)) bitselector_3 (.in(out_3), .out(out_4), .sel(2'b00));

  assign Y = 32'hf4010207;

  // Notes on the sheet:
  //   binary values in Logisim. Convince yourself how the bits are displayed.
  //   Example 2: The bit selector is configured to have 32  
  //   bit group #1 (starting at index 0) is selected for the output.
  //   That is, the 8 bits 0x67 at bit indices 15..8  are sent to the output.
  //   Example 3: Now, assume that you want to extract 3 bits at   
  //   Example 1: A simple example that illustrates how 32-bit values are displayed as 
  //   input bits and 8 output bits. The parameter constant is 1, which means that   
  //   bit indices 10..8. This can be accoplished by putting two bit selecotrs in series.
endmodule

module RegisterFile (
  input  CLK,
  input  [2:0] A1,
  input  [31:0] WD3,
  input  [2:0] A2,
  input  WE3,
  input  [2:0] A3,
  output [31:0] RD1,
  output [31:0] RD2,
  output [31:0] V0
);

  wire and_1_out, and_2_out, and_3_out, and_4_out, and_5_out, and_6_out, and_7_out, decoder_1_out0,
       decoder_1_out1, decoder_1_out2, decoder_1_out3, decoder_1_out4, decoder_1_out5, decoder_1_out6,
       decoder_1_out7;
  wire [31:0] register_1_q, register_2_q, register_4_q, register_5_q, register_6_q, register_7_q,
       register_8_q;

  Decoder #(.select(3)) decoder_1 (
    .out0(decoder_1_out0), .out1(decoder_1_out1), .out2(decoder_1_out2), .out3(decoder_1_out3),
    .out4(decoder_1_out4), .out5(decoder_1_out5), .out6(decoder_1_out6), .out7(decoder_1_out7), .sel(A3));  // open: en
  and and_1 (and_1_out, WE3, decoder_1_out1);
  and and_2 (and_2_out, WE3, decoder_1_out2);
  and and_3 (and_3_out, WE3, decoder_1_out3);
  and and_4 (and_4_out, WE3, decoder_1_out4);
  and and_5 (and_5_out, WE3, decoder_1_out5);
  and and_6 (and_6_out, WE3, decoder_1_out6);
  and and_7 (and_7_out, WE3, decoder_1_out7);
  Register #(.width(32)) register_1 (.D({32{1'b0}}), .Q(register_1_q), .clk(CLK));  // open: en, clr
  Register #(.width(32)) register_2 (.D(WD3), .en(and_1_out), .Q(register_2_q), .clk(CLK));  // open: clr
  Register #(.width(32)) register_3 (.D(WD3), .en(and_2_out), .Q(V0), .clk(CLK));  // open: clr
  Register #(.width(32)) register_4 (.D(WD3), .en(and_3_out), .Q(register_4_q), .clk(CLK));  // open: clr
  Register #(.width(32)) register_5 (.D(WD3), .en(and_4_out), .Q(register_5_q), .clk(CLK));  // open: clr
  Register #(.width(32)) register_6 (.D(WD3), .en(and_5_out), .Q(register_6_q), .clk(CLK));  // open: clr
  Register #(.width(32)) register_7 (.D(WD3), .en(and_6_out), .Q(register_7_q), .clk(CLK));  // open: clr
  Register #(.width(32)) register_8 (.D(WD3), .en(and_7_out), .Q(register_8_q), .clk(CLK));  // open: clr
  Multiplexer #(.select(3), .width(32)) multiplexer_1 (
    .in0(register_1_q), .in1(register_2_q), .in2(V0), .in3(register_4_q), .in4(register_5_q),
    .in5(register_6_q), .in6(register_7_q), .in7(register_8_q), .out(RD1), .sel(A1));  // open: en
  Multiplexer #(.select(3), .width(32)) multiplexer_2 (
    .in0(register_1_q), .in1(register_2_q), .in2(V0), .in3(register_4_q), .in4(register_5_q),
    .in5(register_6_q), .in6(register_7_q), .in7(register_8_q), .out(RD2), .sel(A2));  // open: en
endmodule

module ControlUnit (
  input  [31:0] Instruction,
  output RegDst,
  output RegWrite,
  output ALUSrc,
  output Branch,
  output [2:0] ALUControl
);

  wire comparator_3_eq;
  wire [2:0] bit_extender_1_out;
  wire [5:0] bitselector_1_out;
  wire [31:0] shifter_1_out;

  Shifter #(.width(32), .shift("lr")) shifter_1 (.in(Instruction), .\dist (5'b11010), .out(shifter_1_out));
  BitSelector #(.width(32), .group(6)) bitselector_1 (.in(shifter_1_out), .out(bitselector_1_out), .sel(3'b000));
  Comparator #(.width(6), .mode("unsigned")) comparator_1 (
    .a(bitselector_1_out), .b(6'b001000), .eq(ALUSrc));  // open: gt, lt
  Comparator #(.width(6), .mode("unsigned")) comparator_2 (
    .a(bitselector_1_out), .b({6{1'b0}}), .eq(RegDst));  // open: gt, lt
  Comparator #(.width(6), .mode("unsigned")) comparator_3 (
    .a(bitselector_1_out), .b(6'b000100), .eq(comparator_3_eq));  // open: gt, lt
  assign bit_extender_1_out = {{2{1'b1}}, comparator_3_eq};  // Bit_Extender bit_extender_1
  Shifter #(.width(3)) shifter_2 (.in(bit_extender_1_out), .\dist (2'b01), .out(ALUControl));
  or or_1 (RegWrite, ALUSrc, RegDst);
  and and_1 (Branch, comparator_3_eq, 1'b1);

  // Notes on the sheet:
  //   Zero flag
endmodule
